# Fritzing sketch smartGreenhouse (saved by Fritzing 0.9.3b)
breadboards: 1

parts:
  Part2 = Croduino NOVA
  RHT1 = Humidity and Temperature Sensor RHT03
  R1 = Photocell (LDR) [package=THT]
  LED1 = LED - 5mm [color="Green (565nm)" package="5 mm [THT]"]
  M1 = DC Motor
  J1 = Basic Servo
  J2 = Basic Servo
  R2 = Resistor [tolerance=±5% resistance=10k package=THT]
  R4 = Resistor [tolerance=±5% resistance=4.7k package=THT]
  Q1 = MOSFET-NCHANNEL [package=to220v]
  VCC1 = Battery block 9V  # not connected
  LED2 = LED - 5mm [color="Red (633nm)" package="5 mm [THT]"]
  R5 = Resistor [tolerance=±5% resistance=4.7k package=THT]

nets:
  VCC: Part2.5V, RHT1.Vcc, J1.vcc, J2.vcc
  GND: Part2.GND, RHT1.GND_2, R1.pin_0, LED1.cathode, J1.gnd, J2.gnd, R2.Pin_1, Q1.S, LED2.cathode
  N1: Part2.#13, J2.pulse
  N2: Part2.#12, J1.pulse
  N3: Part2.#14, RHT1.Data-signal
  N4: Part2.#16, R4.Pin_1
  N5: Part2.A, R1.pin_1, R2.Pin_0
  N6: Part2.#5, R5.Pin_1
  N7: Part2.#4, Q1.G
  N8: LED1.anode, R4.Pin_0
  N9: M1.pin_1, Q1.D
  N10: LED2.anode, R5.Pin_0
